// Logisim project Timer24 (1).circ as structural Verilog: 6 circuits, main circuit 计时器
// 16
module \_4位递增计数器  (
  input  Clock,
  input  [3:0] D,
  input  Load,
  input  Enable,
  input  Reset,
  output [3:0] Q
);

  wire and_1_out, and_2_out, and_3_out, multiplexer_1_out, multiplexer_2_out, multiplexer_3_out,
       multiplexer_4_out, xor_1_out, xor_2_out, xor_3_out, xor_4_out, Z;

  and and_1 (and_1_out, Enable, Q[0]);
  and and_2 (and_2_out, and_1_out, Q[1]);
  and and_3 (and_3_out, and_2_out, Q[2]);
  and and_4 (Z, and_3_out, Q[3]);
  xor xor_1 (xor_1_out, Q[0], Enable);
  xor xor_2 (xor_2_out, Q[1], and_1_out);
  xor xor_3 (xor_3_out, Q[2], and_2_out);
  xor xor_4 (xor_4_out, Q[3], and_3_out);
  Multiplexer #(.enable("false")) multiplexer_1 (.in0(xor_1_out), .in1(D[0]), .out(multiplexer_1_out), .sel(Load));
  Multiplexer #(.enable("false")) multiplexer_2 (.in0(xor_2_out), .in1(D[1]), .out(multiplexer_2_out), .sel(Load));
  Multiplexer #(.enable("false")) multiplexer_3 (.in0(xor_3_out), .in1(D[2]), .out(multiplexer_3_out), .sel(Load));
  Multiplexer #(.enable("false")) multiplexer_4 (.in0(xor_4_out), .in1(D[3]), .out(multiplexer_4_out), .sel(Load));
  D_Flip_Flop d_ff_1 (.clk(Clock), .D(multiplexer_1_out), .Q(Q[0]), .reset(Reset));  // open: Qn, preset, en
  D_Flip_Flop d_ff_2 (.clk(Clock), .D(multiplexer_2_out), .Q(Q[1]), .reset(Reset));  // open: Qn, preset, en
  D_Flip_Flop d_ff_3 (.clk(Clock), .D(multiplexer_3_out), .Q(Q[2]), .reset(Reset));  // open: Qn, preset, en
  D_Flip_Flop d_ff_4 (.clk(Clock), .D(multiplexer_4_out), .Q(Q[3]), .reset(Reset));  // open: Qn, preset, en
  Hex_Digit_Display hex_digit_display_1 (.value(Q));  // open: dp

  // Notes on the sheet:
  //   输入引脚
  //   4位二进制（十六进制）同步置数、异步清零功能的同步递增计数器
  //   请勿更改封装外观，否则无法完成测试
  //   输出引脚
  //   监控区
  //   武汉纺织大学数字逻辑课程组
endmodule

// 6
module \六进制计数器  (
  input  Clock,
  input  [3:0] D,
  input  Load,
  input  Enable,
  input  Reset,
  output Co,
  output [3:0] Q
);

  wire and_1_out, or_1_out;

  or or_1 (or_1_out, Co, Load);
  and and_1 (and_1_out, or_1_out, Enable);
  \_4位递增计数器  \u_4位递增计数器_1  (.Clock(Clock), .Enable(Enable), .Reset(Reset), .Q(Q), .D(D), .Load(and_1_out));
  and and_2 (Co, Q[2], Q[0]);
  Hex_Digit_Display hex_digit_display_1 (.value(Q));  // open: dp

  // Notes on the sheet:
  //   输入引脚
  //   六进制计数器
  //   请勿更改封装外观，否则无法完成测试
  //   输出引脚
  //   武汉纺织大学数字逻辑课程组
  //   监控区
endmodule

// 10
module \十进制计数器  (
  input  Clock,
  input  [3:0] D,
  input  Load,
  input  Enable,
  input  Reset,
  output Co,
  output [3:0] Q
);

  wire and_2_out, or_1_out;

  or or_1 (or_1_out, Co, Load);
  and and_1 (Co, Q[3], Q[0]);
  and and_2 (and_2_out, or_1_out, Enable);
  \_4位递增计数器  \u_4位递增计数器_1  (.Clock(Clock), .Enable(Enable), .Reset(Reset), .Q(Q), .D(D), .Load(and_2_out));
  Hex_Digit_Display hex_digit_display_1 (.value(Q));  // open: dp

  // Notes on the sheet:
  //   输入引脚
  //   十进制计数器
  //   请勿更改封装外观，否则无法完成测试
  //   输出引脚
  //   武汉纺织大学数字逻辑课程组
  //   监控区
endmodule

// 60
module \六十进制计数器  (
  input  Clock,
  input  [3:0] D1,
  input  Load,
  input  Enable,
  input  [3:0] D0,
  input  Reset,
  output Co,
  output [3:0] Q1,
  output [3:0] Q0
);

  wire and_1_out, and_2_out, and_3_out, and_4_out, and_5_out, and_6_out, or_1_out, or_2_out, or_3_out;

  and and_1 (and_1_out, Load, Enable);
  and and_2 (and_2_out, Enable, and_6_out);
  or or_1 (or_1_out, and_5_out, Load);
  or or_2 (or_2_out, and_1_out, and_2_out);
  or or_3 (or_3_out, and_6_out, Load);
  and and_3 (and_3_out, or_1_out, Enable);
  \六进制计数器  \u_六进制计数器_1  (
    .Clock(Clock), .D(D1), .Load(and_3_out), .Enable(or_2_out), .Reset(Reset), .Q(Q1));  // open: Co
  and and_4 (and_4_out, or_3_out, Enable);
  \十进制计数器  \u_十进制计数器_1  (.Clock(Clock), .Enable(Enable), .Reset(Reset), .Q(Q0), .Load(and_4_out), .D(D0));  // open: Co
  Hex_Digit_Display hex_digit_display_1 (.value(Q1));  // open: dp
  and and_5 (and_5_out, Q1[2], Q1[0], and_6_out);
  and and_6 (and_6_out, Q0[3], Q0[0]);
  Hex_Digit_Display hex_digit_display_2 (.value(Q0));  // open: dp
  and and_7 (Co, and_6_out, and_5_out);

  // Notes on the sheet:
  //   输入引脚
  //   六十进制计数器
  //   请勿更改封装外观，否则无法完成测试
  //   输出引脚
  //   武汉纺织大学数字逻辑课程组
  //   监控区
endmodule

// 24
module \二十四进制计数器  (
  input  Clock,
  input  [3:0] D1,
  input  Load,
  input  Enable,
  input  [3:0] D0,
  input  Reset,
  output Co,
  output [3:0] Q1,
  output [3:0] Q0
);

  wire and_1_out, and_2_out, and_3_out, and_4_out, and_5_out, and_6_out, and_7_out, and_8_out, or_1_out,
       or_2_out, or_3_out, or_4_out, or_5_out;

  and and_1 (and_1_out, Load, Enable);
  and and_2 (and_2_out, Enable, or_5_out);
  or or_1 (or_1_out, Load, or_5_out);
  or or_2 (or_2_out, and_7_out, Load);
  and and_3 (and_3_out, or_2_out, Enable);
  or or_3 (or_3_out, and_1_out, and_2_out);
  and and_4 (and_4_out, or_1_out, Enable);
  and and_5 (and_5_out, Q1[1], and_8_out);
  or or_4 (or_4_out, and_5_out, and_4_out);
  Hex_Digit_Display hex_digit_display_1 (.value(Q1));  // open: dp
  \十进制计数器  \u_十进制计数器_1  (
    .Clock(Clock), .Enable(or_3_out), .Reset(Reset), .Q(Q1), .Load(and_3_out), .D(D1));  // open: Co
  and and_6 (and_6_out, Q0[3], Q0[0]);
  \十进制计数器  \u_十进制计数器_2  (.Clock(Clock), .Enable(Enable), .Reset(Reset), .Q(Q0), .Load(or_4_out), .D(D0));  // open: Co
  Hex_Digit_Display hex_digit_display_2 (.value(Q0));  // open: dp
  and and_7 (and_7_out, Q1[1], or_5_out);
  or or_5 (or_5_out, and_5_out, and_6_out);
  and and_8 (and_8_out, Q0[1], Q0[0]);
  and and_9 (Co, and_7_out, or_5_out);

  // Notes on the sheet:
  //   输入引脚
  //   二十四进制计数器
  //   请勿更改封装外观，否则无法完成测试
  //   输出引脚
  //   武汉纺织大学数字逻辑课程组
  //   监控区
endmodule

module \计时器  (
  input  Clock,
  input  Load,
  input  [3:0] Dh1,
  input  [3:0] Dh0,
  input  [3:0] Dm1,
  input  [3:0] Dm0,
  input  [3:0] Ds1,
  input  [3:0] Ds0,
  input  Enable,
  input  Reset,
  output [3:0] H1,
  output [3:0] H0,
  output [3:0] M1,
  output [3:0] M0,
  output [3:0] S1,
  output [3:0] S0
);

  wire and_1_out, and_2_out, and_3_out, and_4_out, and_5_out, and_6_out, or_1_out, or_2_out, or_3_out,
       or_4_out, \六十进制计数器_1_co , \六十进制计数器_2_co ;

  Hex_Digit_Display hex_digit_display_1 (.value(H1));  // open: dp
  Hex_Digit_Display hex_digit_display_2 (.value(H0));  // open: dp
  \六十进制计数器  \u_六十进制计数器_1  (
    .Co(\六十进制计数器_1_co ), .Q1(S1), .Q0(S0), .Clock(Clock), .D1(Ds1), .Load(Load), .Enable(Enable),
    .Reset(Reset), .D0(Ds0));
  Hex_Digit_Display hex_digit_display_3 (.value(M1));  // open: dp
  Hex_Digit_Display hex_digit_display_4 (.value(M0));  // open: dp
  and and_1 (and_1_out, Enable, Load);
  or or_1 (or_1_out, Load, \六十进制计数器_1_co );
  and and_2 (and_2_out, Enable, \六十进制计数器_1_co );
  Hex_Digit_Display hex_digit_display_5 (.value(S0));  // open: dp
  Hex_Digit_Display hex_digit_display_6 (.value(S1));  // open: dp
  and and_3 (and_3_out, or_1_out, Load);
  or or_2 (or_2_out, and_2_out, and_1_out);
  \六十进制计数器  \u_六十进制计数器_2  (
    .Co(\六十进制计数器_2_co ), .Q1(M1), .Q0(M0), .Clock(Clock), .D1(Dm1), .Load(and_3_out), .Enable(or_2_out),
    .Reset(Reset), .D0(Dm0));
  or or_3 (or_3_out, Load, \六十进制计数器_2_co );
  and and_4 (and_4_out, \六十进制计数器_1_co , Enable, \六十进制计数器_2_co );
  and and_5 (and_5_out, Enable, Load);
  and and_6 (and_6_out, or_3_out, Load);
  or or_4 (or_4_out, and_4_out, and_5_out);
  \二十四进制计数器  \u_二十四进制计数器_1  (
    .Clock(Clock), .D1(Dh1), .Load(and_6_out), .Q1(H1), .Q0(H0), .Enable(or_4_out), .D0(Dh0), .Reset(Reset));  // open: Co

  // Notes on the sheet:
  //   二十四小时计时器
  //   请勿更改封装外观，否则无法完成测试
  //   :
  //   输入引脚
  //   :
  //   输出引脚
  //   武汉纺织大学数字逻辑课程组
endmodule
